# Fritzing sketch diagram1 (saved by Fritzing 0.9.3b)
circuit board: 33.556cm x 22.622cm

parts:
  MCU1 = Raspberry Pi Zero
  RGB_Strip_LED2 = RGB Strip LED
  JACK2 = 2.1mm Barrel Jack with Terminal Block [part_number="12 V"]
  R4 = Resistor [tolerance=±5% resistance=1.5k package=THT]
  Q1 = Basic FET N-Channel [package="TO220 [THT]"]

nets (from the breadboard view):
  N1: MCU1.pin_22, R4.Pin_0, Q1.gate
  N2: RGB_Strip_LED2.Common_Connect, JACK2.POS
  N3: RGB_Strip_LED2.Blue_Connect, Q1.source
  N4: JACK2.NEG, R4.Pin_1, Q1.drain

notes:
  IRLZ34N

custom parts:
  RGB Strip LED: A tri-color Strip LED with red, green and blue. Based on LED SMD 5050 RGB Pin order: common cathode - green - red - blue
